# Fritzing sketch diagram (saved by Fritzing 0.9.2b)
breadboards: 1

parts:
  Raspberry_Pi_Model_B+ = Raspberry Pi B+  # not connected
  servomotor = Basic Servo
  Arduino_Uno_Rev3 = Arduino Uno (Rev3)
  PIR_HC-SR501 = HC-SR501 Body Sensor Module

nets:
  GND: servomotor.gnd, Arduino_Uno_Rev3.GND, PIR_HC-SR501.GND
  VCC: servomotor.vcc, Arduino_Uno_Rev3.5V, PIR_HC-SR501.VCC
  N1: servomotor.pulse, Arduino_Uno_Rev3.D4
  N2: Arduino_Uno_Rev3.D2, PIR_HC-SR501.OUT

notes:
  webcam
  arduino
  raspberry

custom parts:
  HC-SR501 Body Sensor Module: Pyroelectric Infrared PIR Motion Sensor Detector Module
